// Digital circuit 4bit_CPU.dig as structural Verilog
module _4bit_CPU (
);

  wire Counter_p1, IR_p2, ramblock_1_p3;

  // ProgramCounter Counter: pin names not known; wires that end beside it: Counter_p1
  // ramBlock ramblock_1: pin names not known; wires that end beside it: Counter_p1, Counter_p1, ramblock_1_p3
  // Register IR: pin names not known; wires that end beside it: ramblock_1_p3, IR_p2
  // _4bit_ALU _4bit_alu_1: pin names not known; wires that end beside it: IR_p2
  RegisterFile registerfile_1 ();  // open: Clock, Clear, Zero_Flag, Clear_2, Zero_Flag_2, Write_Register, Write_Data, Read_Data_A, Read_data_B
endmodule
