// Digital circuit IR.dig as structural Verilog
module IR (
  input  [3:0] Data,
  input  Clock,
  output [2:0] Instruction
);

  wire [3:3] register_1_p3;

  // Register register_1: pin names not known; wires that end beside it: Clock, Data, {register_1_p3[3], Instruction}
endmodule
