// Digital circuit RegisterFile.dig as structural Verilog
module RegisterFile (
  input  Clock,
  input  [3:0] Clear,
  input  Zero_Flag,
  input  [3:0] Clear_2,
  input  Zero_Flag_2,
  input  Write_Register,
  input  [3:0] Write_Data,
  output [3:0] Read_Data_A,
  output [3:0] Read_data_B
);

  wire demultiplexer_2_out_0, demultiplexer_2_out_1;
  wire [3:0] and_1_out, and_2_out, demultiplexer_1_out_0, demultiplexer_1_out_1, multiplexer_1_out,
       multiplexer_2_out;

  Demultiplexer #(.Bits(4)) demultiplexer_1 (
    .sel(Write_Register), .in(Write_Data), .out_0(demultiplexer_1_out_0), .out_1(demultiplexer_1_out_1));
  Demultiplexer demultiplexer_2 (
    .sel(Write_Register), .in(1'b1), .out_0(demultiplexer_2_out_0), .out_1(demultiplexer_2_out_1));
  assign and_1_out = demultiplexer_1_out_0 & multiplexer_1_out;  // And and_1, 4 bits wide
  assign and_2_out = demultiplexer_1_out_1 & multiplexer_2_out;  // And and_2, 4 bits wide
  Multiplexer #(.Bits(4)) multiplexer_1 (
    .sel(Zero_Flag), .in_0(demultiplexer_1_out_0), .in_1(Clear), .out(multiplexer_1_out));
  Register #(.Bits(4)) A (.D(and_1_out), .C(Clock), .en(demultiplexer_2_out_0), .Q(Read_Data_A));
  Multiplexer #(.Bits(4)) multiplexer_2 (
    .sel(Zero_Flag_2), .in_0(demultiplexer_1_out_1), .in_1(Clear_2), .out(multiplexer_2_out));
  Register #(.Bits(4)) A_2 (.D(and_2_out), .C(Clock), .en(demultiplexer_2_out_1), .Q(Read_data_B));
endmodule
